# Fritzing sketch 3blinks (saved by Fritzing 0.9.3b)
breadboards: 1

parts:
  R1 = Resistor [tolerance=±5% resistance=220 package=THT]
  LED1 = LED - 5mm [color="Blue (470nm)" package="5 mm [THT]"]
  Part1 = Arduino Uno (Rev3)
  R2 = Resistor [tolerance=±5% resistance=220 package=THT]
  LED2 = LED - 5mm [color="Red (633nm)" package="5 mm [THT]"]
  R3 = Resistor [tolerance=±5% resistance=220 package=THT]
  LED3 = LED - 5mm [color="Green (560nm)" package="5 mm [THT]"]

nets:
  N1: R1.Pin_0, LED1.anode
  N2: R1.Pin_1, Part1.D12/MISO
  N3: LED1.cathode, Part1.GND, LED2.cathode, LED3.cathode
  N4: Part1.D10_PWM/SS, R3.Pin_1
  N5: Part1.D11_PWM/MOSI, R2.Pin_1
  N6: R2.Pin_0, LED2.anode
  N7: R3.Pin_0, LED3.anode
