# Fritzing sketch blinking_led (saved by Fritzing 0.9.3b)
breadboards: 1

parts:
  Part1 = Arduino Uno (Rev3)
  R1 = Resistor [tolerance=±5% resistance=220 package=THT]
  LED1 = LED - 3mm [color="Blue (470nm)" package="3 mm [THT]"]
  R2 = Resistor [tolerance=±5% resistance=220 package=THT]

nets:
  N1: Part1.D2, R2.Pin_1
  N2: Part1.GND, LED1.cathode
  N3: R1.Pin_0, LED1.anode
  N4: R1.Pin_1, R2.Pin_0
